# Fritzing sketch aga_clock-big-sound (saved by Fritzing 0.9.3b)
breadboards: 2

parts:
  パーツ1 = Arduino Uno (Rev3)
  DFPlayer_Mini1 = DFPlayer MINI [package="DIP (Dual Inline) [THT]"]
  SPKR1 = Loudspeaker
  R1 = Resistor [tolerance=±5% resistance=1k package=THT]
  U1 = 74HC595 [package="DIP16 [THT]"]
  7_Segment2 = 7 Segment Display
  7_Segment3 = 7 Segment Display
  7_Segment4 = 7 Segment Display
  7_Segment5 = 7 Segment Display
  RTC1 = RTC-8564NB [package="Module(DIP 8P)"]
  S3 = Momentary Switch [package=tactile-pth]
  R2 = Resistor [tolerance=±5% resistance=1k package=THT]
  R3 = Resistor [tolerance=±5% resistance=1k package=THT]
  R4 = Resistor [tolerance=±5% resistance=1k package=THT]

nets:
  N1: パーツ1.D8, 7_Segment2.common_cathode
  N2: パーツ1.D9_PWM, 7_Segment3.common_cathode
  N3: パーツ1.D10_PWM/SS, 7_Segment5.common_cathode
  N4: パーツ1.D11_PWM/MOSI, 7_Segment4.common_cathode
  GND: パーツ1.GND, DFPlayer_Mini1.GND#6, U1.GND, U1.OE, RTC1.GND, R2.Pin_0
  N5: パーツ1.A4/SDA, R3.Pin_1
  N6: パーツ1.A5/SCL, R4.Pin_1
  N7: パーツ1.D0/RX, DFPlayer_Mini1.TX
  N8: パーツ1.D1/TX, R1.Pin_1
  N9: パーツ1.D5_PWM, U1.SH_CP
  N10: パーツ1.D6_PWM, U1.ST_CP
  N11: パーツ1.D7, U1.DS
  VCC: パーツ1.3V3, DFPlayer_Mini1.VCC, U1.MR, U1.VCC, RTC1.VDD, S3.3
  N12: DFPlayer_Mini1.RX, R1.Pin_0
  N13: DFPlayer_Mini1.SPK1, SPKR1.pin2
  N14: DFPlayer_Mini1.SPK2, SPKR1.pin1
  N15: U1.Q1, 7_Segment2.Segment_B
  N16: U1.Q2, 7_Segment2.Segment_C
  N17: U1.Q3, 7_Segment2.Segment_D
  N18: U1.Q4, 7_Segment2.Segment_E
  N19: U1.Q5, 7_Segment2.Segment_F
  N20: U1.Q6, 7_Segment2.Segment_G
  N21: U1.Q0, 7_Segment2.Segment_A
  N22: RTC1.SDA, R3.Pin_0
  N23: RTC1.SCL, R4.Pin_0
  N24: S3.4, R2.Pin_1

custom parts:
  DFPlayer MINI: MP3 module by DFRobot.com for playing Music from an SD-Card. Supports WAV and MP3 files.
  RTC-8564NB: Real Time Clock Module and I2C-BUS interface method. This product is a module of the SON 8-pin DIP package. Supply voltage 1.8-5.5V original version by KimuShige
